# Fritzing sketch circuit (saved by Fritzing 0.9.10b)
breadboards: 1

parts:
  Mod1 = Raspberry Pi 4B
  Part1 = BME280 Breakout
  Chirp!_Soil_Moisture_Sensor1 = Chirp! Soil Moisture Sensor v2.7.3  # not connected
  Chirp!_Soil_Moisture_Sensor2 = Chirp! Soil Moisture Sensor v2.7.3  # not connected
  Chirp!_Soil_Moisture_Sensor3 = Chirp! Soil Moisture Sensor v2.7.3  # not connected
  Part2 = Adafruit ADS1015 12Bit I2C ADC [part_number="Adafruit #1083"]  # not connected

nets:
  3V3: Mod1.3V3, Part1.3.3V
  N1: Mod1.GPIO2, Part1.SCK/SCL
  N2: Mod1.GPIO3, Part1.SDI/SDA
  GND: Mod1.GND, Part1.GND

custom parts:
  Adafruit ADS1015 12Bit I2C ADC: For microcontrollers without an analog-to-digital converter or when you want a higher-precision ADC, the ADS1015 provides 12-bit precision at 3300 samples/second over I2C. The chip can be configured as 4 single-ended input channels, or two differential channels. As a nice bonus, it even includes a programmable gain amplifier, up to x16, to help boost up smaller single/differential signals to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
